# Fritzing sketch DarthStep (saved by Fritzing 0.7.10b)
breadboards: 2

parts:
  U1 = Arduino Mega
  R1 = Rotary Potentiometer (Small) [maximum_resistance=10kΩ]
  R2 = Rotary Potentiometer (Small) [maximum_resistance=10kΩ]
  S4 = Pushbutton [package="[THT]"]
  S3 = Pushbutton [package="[THT]"]
  S2 = Pushbutton [package="[THT]"]
  S1 = Pushbutton [package="[THT]"]
  R3 = Photocell (LDR) [package=THT]
  R4 = Resistor [tolerance=±5% resistance=10k package=THT]
  GLCD_128x64 = 128 x 64 Graphic LCD
  DIN1 = DIN-5 jack (MIDI) [package=THT]
  R6 = Resistor [tolerance=±5% resistance=220 package=THT]
  R7 = Resistor [tolerance=±5% resistance=20k package=THT]
  R8 = Resistor [tolerance=±5% resistance=10k package=THT]
  R9 = Resistor [tolerance=±5% resistance=10k package=THT]
  R10 = Resistor [tolerance=±5% resistance=10k package=THT]
  R11 = Resistor [tolerance=±5% resistance=10k package=THT]
  R12 = Resistor [tolerance=±5% resistance=10k package=THT]
  R13 = Resistor [tolerance=±5% resistance=10k package=THT]
  R14 = Resistor [tolerance=±5% resistance=10k package=THT]
  R15 = Resistor [tolerance=±5% resistance=20k package=THT]
  R16 = Resistor [tolerance=±5% resistance=20k package=THT]
  R17 = Resistor [tolerance=±5% resistance=20k package=THT]
  R18 = Resistor [tolerance=±5% resistance=20k package=THT]
  R19 = Resistor [tolerance=±5% resistance=20k package=THT]
  R20 = Resistor [tolerance=±5% resistance=20k package=THT]
  R21 = Resistor [tolerance=±5% resistance=10k package=THT]
  R22 = Resistor [tolerance=±5% resistance=20k package=THT]
  R23 = Resistor [tolerance=±5% resistance=10k package=THT]
  IC1 = IC, DIP package, 8 pins [chip_label=LM386]
  R24 = Resistor [tolerance=±5% resistance=20k package=THT]
  C1 = Electrolytic Capacitor [capacitance=22µF voltage=35V package="100 mil [THT, electrolytic]"]
  C2 = Electrolytic Capacitor [capacitance=22µF voltage=35V package="100 mil [THT, electrolytic]"]
  R25 = Rotary Potentiometer (Small) [maximum_resistance=10kΩ]
  R26 = Resistor [tolerance=±5% resistance=4.7k package=THT]
  R27 = Rotary Potentiometer (Small) [maximum_resistance=10kΩ]
  R28 = Resistor [tolerance=±5% resistance=220 package=THT]
  SPKR1 = Loudspeaker
  VCC1 = Battery block 9V

nets:
  GND: U1.GND, U1.VIN, R1.leg2, R2.leg2, S4.Pin_3, S4.Pin_4, S3.Pin_3, S3.Pin_4, S2.Pin_3, S2.Pin_4, S1.Pin_3, S1.Pin_4, R4.Pin_0, GLCD_128x64.20_K(-), DIN1.2, R21.Pin_0, IC1.pin2, IC1.pin4, IC1.pin6, R25.leg2, R26.Pin_0, R27.leg1, R28.Pin_0, SPKR1.pin1, VCC1.-, VCC1.+
  N1: U1.+5V#18, R1.leg1, R2.leg1, R3.pin_1, R6.Pin_0
  N2: U1.A0, R3.pin_0, R4.Pin_1
  N3: U1.A1, R1.wiper
  N4: U1.A2, R2.wiper
  N5: U1.D14, DIN1.5
  N6: U1.D22, R7.Pin_1
  N7: U1.D23, R15.Pin_1
  N8: U1.D24, R16.Pin_1
  N9: U1.D25, R17.Pin_1
  N10: U1.D26, R18.Pin_1
  N11: U1.D27, R19.Pin_1
  N12: U1.D28, R20.Pin_1
  N13: U1.D29, R22.Pin_1
  N14: U1.D30, GLCD_128x64.17_RST
  N15: U1.D31, GLCD_128x64.16_CS2
  N16: U1.D32, GLCD_128x64.15_CS1
  N17: U1.D33, GLCD_128x64.14_DB7
  N18: U1.D34, GLCD_128x64.13_DB6
  N19: U1.D35, GLCD_128x64.12_DB5
  N20: U1.D36, GLCD_128x64.11_DB4
  N21: U1.D37, GLCD_128x64.10_DB3
  N22: U1.D38, GLCD_128x64.9_BD2
  N23: U1.D39, GLCD_128x64.8_DB1
  N24: U1.D40, GLCD_128x64.7_DB0
  N25: U1.D41, GLCD_128x64.6_Enable
  N26: U1.D42, GLCD_128x64.5_R/W
  N27: U1.D43, GLCD_128x64.4_D/I
  N28: U1.D44, S1.Pin_1, S1.Pin_2
  N29: U1.D45, S2.Pin_1, S2.Pin_2
  N30: U1.D46, S3.Pin_1, S3.Pin_2
  N31: U1.D47, S4.Pin_1, S4.Pin_2
  N32: U1.+5V#80, GLCD_128x64.2_Vdd, GLCD_128x64.19_A(+)
  N33: GLCD_128x64.1_Vss, R28.Pin_1
  N34: GLCD_128x64.3_Vo, R27.leg2
  N35: GLCD_128x64.18_Vout, R27.wiper
  N36: DIN1.4, R6.Pin_1
  N37: R7.Pin_0, R8.Pin_1, R21.Pin_1
  N38: R8.Pin_0, R9.Pin_1, R15.Pin_0
  N39: R9.Pin_0, R10.Pin_1, R16.Pin_0
  N40: R10.Pin_0, R11.Pin_1, R17.Pin_0
  N41: R11.Pin_0, R12.Pin_1, R18.Pin_0
  N42: R12.Pin_0, R13.Pin_1, R19.Pin_0
  N43: R13.Pin_0, R14.Pin_1, R20.Pin_0
  N44: R14.Pin_0, R22.Pin_0, R23.Pin_1
  N45: R23.Pin_0, C1.+
  N46: IC1.pin3, R24.Pin_0, R26.Pin_1
  N47: IC1.pin5, C2.+
  N48: R24.Pin_1, C1.-
  N49: C2.-, R25.leg1
  N50: R25.wiper, SPKR1.pin2
